# Fritzing sketch BeeHive (saved by Fritzing 1.0.8)
circuit board: 8.46667cm x 5.64444cm
stripboards: 2

parts:
  INA226 = ina226 module
  BATTERY = LIPO-2000mAh [package=lipo-2000]
  CN3065 = CN3065 Mini Solar Charger Module
  PANEL = SOLAR-IXYS [package=solarbit-12x1]
  NAU7802 = Adafruit NAU7802 Breakout Rev C [mn=Adafruit mpn=#4538 part_number=#4538]
  FeatherS3D = featherS3
  SHT40 = SHT40 Breakout [mn=Sensirion package="Breakout Module [THT]"]
  C1 = Electrolytic Capacitor [capacitance=470µF voltage=6.3V package="200 mil [THT, electrolytic]"]
  C2 = Ceramic Capacitor [capacitance=100nF voltage=35V package="100 mil [THT, multilayer]"]
  C3 = Ceramic Capacitor [capacitance=100nF voltage=35V package="100 mil [THT, multilayer]"]
  INMP441 = INMP441
  J_SOLAR = female pin header, 2 pins [form="♀ (female)"]
  J_CHG = female pin header, 2 pins [form="♀ (female)"]
  J_PWR = female pin header, 2 pins [form="♀ (female)"]
  J_HIVE = female pin header, 8 pins [form="♀ (female)"]
  J_SUB = female pin header, 8 pins [form="♀ (female)"]

nets:
  N1: INA226.Pin_1, PANEL.A, J_SOLAR.pin1
  N2: INA226.Pin_2, INA226.Pin_3, CN3065.Pin_1, J_CHG.pin1
  N3: INA226.Pin_5, NAU7802.SCL, FeatherS3D.Pin_22, SHT40.SCL, J_HIVE.pin3, J_SUB.pin3
  N4: INA226.Pin_6, NAU7802.SDA, FeatherS3D.Pin_21, SHT40.SDA, J_HIVE.pin2, J_SUB.pin2
  GND: INA226.Pin_7, BATTERY.-, CN3065.Pin_2, CN3065.Pin_8, CN3065.Pin_10, PANEL.C, NAU7802.GND, FeatherS3D.Pin_4, FeatherS3D.Pin_17, FeatherS3D.Pin_19, FeatherS3D.Pin_33, FeatherS3D.Pin_38, SHT40.GND, C1.-, C2.0, C3.0, INMP441.L/R, INMP441.GND, J_SOLAR.pin2, J_CHG.pin2, J_PWR.pin2, J_HIVE.pin4, J_HIVE.pin5, J_SUB.pin4, J_SUB.pin5
  VCC: INA226.Pin_8, NAU7802.VCC, FeatherS3D.Pin_16, SHT40.VIN, C2.1, C3.1, INMP441.VDD, J_HIVE.pin1, J_SUB.pin1
  N5: BATTERY.+, CN3065.Pin_7, CN3065.Pin_9, FeatherS3D.Pin_32, C1.+, J_PWR.pin1
  N6: FeatherS3D.Pin_25, INMP441.WS, J_HIVE.pin6, J_SUB.pin6
  N7: FeatherS3D.Pin_26, INMP441.SCK, J_HIVE.pin7, J_SUB.pin7
  N8: FeatherS3D.Pin_27, INMP441.SD, J_HIVE.pin8, J_SUB.pin8

custom parts:
  ina226 module: INA226 Voltage Current/Power Monitoring Sensor Module IIC I2C Interface Bi-directional INA226 Module CJMCU-226.
  CN3065 Mini Solar Charger Module: Fc-51 Infrared Obstacle Avoidance Proximity Sensor module. IR transmitter led, receiver LED, lm393 compaitor and a pot. 3.3 V to 5V power.
  featherS3: FeatherS3 is the latest in our super popular ESP32 based Feather boards.
  SHT40 Breakout: SHT40 Temperature and Humidity Sensor Breakout Module. Sensirion SHT40 with I2C interface (address 0x44). 10mm x 13mm purple PCB with 4-pin header (VIN, GND, SCL, SDA).
  INMP441: This is a simple breakout board for the INMP441 I2S MEMS microphone.
